// Logisim project Banco de Registradores.circ as structural Verilog: 1 circuit, main circuit Banco de Registradores
module Banco_de_Registradores (
  input  RegWrite,
  input  [4:0] WR,
  input  [31:0] WD,
  input  [4:0] LR1,
  input  [4:0] LR2,
  output [31:0] LD1,
  output [31:0] LD2
);

  wire and_1_out, and_2_out, and_3_out, and_4_out, and_5_out, and_6_out, and_7_out, and_8_out, and_9_out,
       and_10_out, and_11_out, and_12_out, and_13_out, and_14_out, and_15_out, and_16_out, and_17_out,
       and_18_out, and_19_out, and_20_out, and_21_out, and_22_out, and_23_out, and_24_out, and_25_out,
       and_26_out, and_27_out, and_28_out, and_29_out, and_30_out, and_31_out, decoder_1_out1,
       decoder_1_out2, decoder_1_out3, decoder_1_out4, decoder_1_out5, decoder_1_out6, decoder_1_out7,
       decoder_1_out8, decoder_1_out9, decoder_1_out10, decoder_1_out11, decoder_1_out12, decoder_1_out13,
       decoder_1_out14, decoder_1_out15, decoder_1_out16, decoder_1_out17, decoder_1_out18, decoder_1_out19,
       decoder_1_out20, decoder_1_out21, decoder_1_out22, decoder_1_out23, decoder_1_out24, decoder_1_out25,
       decoder_1_out26, decoder_1_out27, decoder_1_out28, decoder_1_out29, decoder_1_out30, decoder_1_out31;
  wire [31:0] _0, _1, _2, _3, _4, _5, _6, _7, _8, _9, _10, _11, _12, _13, _14, _15, _16, _17, _18, _19, _20,
       _21, _22, _23, _24, _25, _26, _27, _28, _29, _30, _31;

  Register #(.width(32)) register_1 (.D(WD), .Q(_0));  // open: en, clk, clr
  Decoder #(.select(5)) decoder_1 (
    .out1(decoder_1_out1), .out2(decoder_1_out2), .out3(decoder_1_out3), .out4(decoder_1_out4),
    .out5(decoder_1_out5), .out6(decoder_1_out6), .out7(decoder_1_out7), .out8(decoder_1_out8),
    .out9(decoder_1_out9), .out10(decoder_1_out10), .out11(decoder_1_out11), .out12(decoder_1_out12),
    .out13(decoder_1_out13), .out14(decoder_1_out14), .out15(decoder_1_out15), .out16(decoder_1_out16),
    .out17(decoder_1_out17), .out18(decoder_1_out18), .out19(decoder_1_out19), .out20(decoder_1_out20),
    .out21(decoder_1_out21), .out22(decoder_1_out22), .out23(decoder_1_out23), .out24(decoder_1_out24),
    .out25(decoder_1_out25), .out26(decoder_1_out26), .out27(decoder_1_out27), .out28(decoder_1_out28),
    .out29(decoder_1_out29), .out30(decoder_1_out30), .out31(decoder_1_out31), .sel(WR));  // open: out0, en
  Register #(.width(32)) register_2 (.D(WD), .Q(_1), .clk(and_1_out));  // open: en, clr
  and and_1 (and_1_out, RegWrite, decoder_1_out1);
  Register #(.width(32)) register_3 (.D(WD), .Q(_31), .clk(and_2_out));  // open: en, clr
  and and_2 (and_2_out, decoder_1_out31, RegWrite);
  and and_3 (and_3_out, RegWrite, decoder_1_out2);
  and and_4 (and_4_out, decoder_1_out30, RegWrite);
  Register #(.width(32)) register_4 (.D(WD), .Q(_2), .clk(and_3_out));  // open: en, clr
  and and_5 (and_5_out, RegWrite, decoder_1_out3);
  Register #(.width(32)) register_5 (.D(WD), .Q(_30), .clk(and_4_out));  // open: en, clr
  and and_6 (and_6_out, decoder_1_out29, RegWrite);
  Register #(.width(32)) register_6 (.D(WD), .Q(_3), .clk(and_5_out));  // open: en, clr
  and and_7 (and_7_out, RegWrite, decoder_1_out4);
  Register #(.width(32)) register_7 (.D(WD), .Q(_29), .clk(and_6_out));  // open: en, clr
  Register #(.width(32)) register_8 (.D(WD), .Q(_4), .clk(and_7_out));  // open: en, clr
  Register #(.width(32)) register_9 (.D(WD), .Q(_28), .clk(and_8_out));  // open: en, clr
  and and_8 (and_8_out, decoder_1_out28, RegWrite);
  Register #(.width(32)) register_10 (.D(WD), .Q(_5), .clk(and_9_out));  // open: en, clr
  and and_9 (and_9_out, RegWrite, decoder_1_out5);
  Register #(.width(32)) register_11 (.D(WD), .Q(_27), .clk(and_10_out));  // open: en, clr
  and and_10 (and_10_out, decoder_1_out27, RegWrite);
  Register #(.width(32)) register_12 (.D(WD), .Q(_6), .clk(and_11_out));  // open: en, clr
  and and_11 (and_11_out, RegWrite, decoder_1_out6);
  Register #(.width(32)) register_13 (.D(WD), .Q(_26), .clk(and_12_out));  // open: en, clr
  and and_12 (and_12_out, decoder_1_out26, RegWrite);
  Register #(.width(32)) register_14 (.D(WD), .Q(_7), .clk(and_13_out));  // open: en, clr
  and and_13 (and_13_out, RegWrite, decoder_1_out7);
  Register #(.width(32)) register_15 (.D(WD), .Q(_25), .clk(and_14_out));  // open: en, clr
  and and_14 (and_14_out, decoder_1_out25, RegWrite);
  Register #(.width(32)) register_16 (.D(WD), .Q(_8), .clk(and_15_out));  // open: en, clr
  and and_15 (and_15_out, RegWrite, decoder_1_out8);
  Register #(.width(32)) register_17 (.D(WD), .Q(_24), .clk(and_16_out));  // open: en, clr
  and and_16 (and_16_out, decoder_1_out24, RegWrite);
  Register #(.width(32)) register_18 (.D(WD), .Q(_9), .clk(and_17_out));  // open: en, clr
  and and_17 (and_17_out, RegWrite, decoder_1_out9);
  Register #(.width(32)) register_19 (.D(WD), .Q(_23), .clk(and_18_out));  // open: en, clr
  and and_18 (and_18_out, decoder_1_out23, RegWrite);
  and and_19 (and_19_out, RegWrite, decoder_1_out10);
  and and_20 (and_20_out, decoder_1_out22, RegWrite);
  Multiplexer #(.select(5), .width(32)) multiplexer_1 (
    .in0(_0), .in1(_1), .in2(_2), .in3(_3), .in4(_4), .in5(_5), .in6(_6), .in7(_7), .in8(_8), .in9(_9),
    .in10(_10), .in11(_11), .in12(_12), .in13(_13), .in14(_14), .in15(_15), .in16(_16), .in17(_17),
    .in18(_18), .in19(_19), .in20(_20), .in21(_21), .in22(_22), .in23(_23), .in24(_24), .in25(_25),
    .in26(_26), .in27(_27), .in28(_28), .in29(_29), .in30(_30), .in31(_31), .out(LD1), .sel(LR1));  // open: en
  Multiplexer #(.select(5), .width(32)) multiplexer_2 (
    .in0(_0), .in1(_1), .in2(_2), .in3(_3), .in4(_4), .in5(_5), .in6(_6), .in7(_7), .in8(_8), .in9(_9),
    .in10(_10), .in11(_11), .in12(_12), .in13(_13), .in14(_14), .in15(_15), .in16(_16), .in17(_17),
    .in18(_18), .in19(_19), .in20(_20), .in21(_21), .in22(_22), .in23(_23), .in24(_24), .in25(_25),
    .in26(_26), .in27(_27), .in28(_28), .in29(_29), .in30(_30), .in31(_31), .out(LD2), .sel(LR2));  // open: en
  Register #(.width(32)) register_20 (.D(WD), .Q(_10), .clk(and_19_out));  // open: en, clr
  and and_21 (and_21_out, RegWrite, decoder_1_out11);
  Register #(.width(32)) register_21 (.D(WD), .Q(_22), .clk(and_20_out));  // open: en, clr
  and and_22 (and_22_out, decoder_1_out21, RegWrite);
  Register #(.width(32)) register_22 (.D(WD), .Q(_11), .clk(and_21_out));  // open: en, clr
  and and_23 (and_23_out, RegWrite, decoder_1_out12);
  Register #(.width(32)) register_23 (.D(WD), .Q(_21), .clk(and_22_out));  // open: en, clr
  Register #(.width(32)) register_24 (.D(WD), .Q(_12), .clk(and_23_out));  // open: en, clr
  Register #(.width(32)) register_25 (.D(WD), .Q(_20), .clk(and_24_out));  // open: en, clr
  and and_24 (and_24_out, decoder_1_out20, RegWrite);
  Register #(.width(32)) register_26 (.D(WD), .Q(_13), .clk(and_25_out));  // open: en, clr
  and and_25 (and_25_out, RegWrite, decoder_1_out13);
  Register #(.width(32)) register_27 (.D(WD), .Q(_19), .clk(and_26_out));  // open: en, clr
  and and_26 (and_26_out, decoder_1_out19, RegWrite);
  Register #(.width(32)) register_28 (.D(WD), .Q(_14), .clk(and_27_out));  // open: en, clr
  and and_27 (and_27_out, RegWrite, decoder_1_out14);
  Register #(.width(32)) register_29 (.D(WD), .Q(_18), .clk(and_28_out));  // open: en, clr
  and and_28 (and_28_out, decoder_1_out18, RegWrite);
  Register #(.width(32)) register_30 (.D(WD), .Q(_15), .clk(and_29_out));  // open: en, clr
  and and_29 (and_29_out, RegWrite, decoder_1_out15);
  Register #(.width(32)) register_31 (.D(WD), .Q(_17), .clk(and_30_out));  // open: en, clr
  and and_30 (and_30_out, decoder_1_out17, RegWrite);
  Register #(.width(32)) register_32 (.D(WD), .Q(_16), .clk(and_31_out));  // open: en, clr
  and and_31 (and_31_out, decoder_1_out16, RegWrite);
endmodule
