// Logisim project ULA 32 bits.circ as structural Verilog: 1 circuit, main circuit ULA
module ULA (
  input  [31:0] A,
  input  [31:0] B,
  input  [3:0] \Operação_ALU ,
  input  [4:0] shamt,
  output ZERO,
  output [31:0] Result,
  output Overflow
);

  wire and_2_out, and_3_out, and_4_out, and_5_out, and_6_out, and_7_out, and_8_out, and_9_out, or_2_out,
       or_3_out, or_4_out, or_5_out;
  wire [0:0] SLT;
  wire [30:0] and_10_out;
  wire [31:0] ADD, AND, NOR, OR, SLL, SRL, SUB, XOR;

  assign AND = A & B;  // AND_Gate and_1, 32 bits wide
  assign OR = A | B;  // OR_Gate or_1, 32 bits wide
  assign NOR = ~(A | B);  // NOR_Gate nor_1, 32 bits wide
  assign XOR = A ^ B;  // XOR_Gate xor_1, 32 bits wide
  Comparator #(.width(32)) comparator_1 (.a(A), .b(B), .lt(SLT[0]));  // open: gt, eq
  Adder #(.width(32)) adder_1 (.a(A), .b(B), .out(ADD));  // open: cin, cout
  Subtractor #(.width(32)) subtractor_1 (.a(A), .b(B), .out(SUB));  // open: bin, bout
  Shifter #(.width(32)) shifter_1 (.in(A), .\dist (shamt), .out(SLL));
  Shifter #(.width(32), .shift("lr")) shifter_2 (.in(A), .\dist (shamt), .out(SRL));
  Multiplexer #(.select(4), .width(32)) multiplexer_1 (
    .in0(AND), .in1(OR), .in2(NOR), .in3(XOR), .in4({{31{1'b0}}, SLT[0]}), .in5(ADD), .in6(SUB), .in7(SLL),
    .in8(SRL), .out(Result), .sel(\Operação_ALU ));  // open: in9, in10, in11, in12, in13, in14, in15, en
  and and_2 (and_2_out, ~A[31], ~B[31], Result[31]);  // AND_Gate
  and and_3 (and_3_out, A[31], B[31], ~Result[31]);  // AND_Gate
  and and_4 (and_4_out, ~A[31], B[31], Result[31]);  // AND_Gate
  and and_5 (and_5_out, A[31], ~B[31], ~Result[31]);  // AND_Gate
  or or_2 (or_2_out, and_2_out, and_3_out);
  and and_6 (and_6_out, or_2_out, ~\Operação_ALU [1]);  // AND_Gate
  and and_7 (and_7_out, \Operação_ALU [1], or_3_out);
  or or_3 (or_3_out, and_4_out, and_5_out);
  and and_8 (and_8_out, ~\Operação_ALU [3], \Operação_ALU [2], ~\Operação_ALU [1], \Operação_ALU [0]);  // AND_Gate
  and and_9 (and_9_out, ~\Operação_ALU [3], \Operação_ALU [2], \Operação_ALU [1], ~\Operação_ALU [0]);  // AND_Gate
  assign {ZERO, and_10_out} = {32{1'b1}} & ~Result;  // AND_Gate and_10, 32 bits wide
  or or_4 (or_4_out, and_6_out, and_7_out);
  or or_5 (or_5_out, and_8_out, and_9_out);
  and and_11 (Overflow, or_4_out, or_5_out);

  // Other names for the same wires on the sheet: op[3:0] = \Operação_ALU ; res[31:0] = Result

  // Notes on the sheet:
  //   lógicas
  //   aritiméticas
endmodule
