// Logisim project Decodificador de Instruções.circ as structural Verilog: 1 circuit, main circuit Decodificador de Instruções
module \Decodificador_de_Instruções  (
  input  [31:0] \instrução ,
  output [4:0] rs,
  output [4:0] rt,
  output [4:0] rd,
  output [4:0] shamt,
  output [4:0] funct,
  output [15:0] imm,
  output [25:0] addr,
  output [5:0] opcode
);

  wire J, JAL, not_1_out, or_1_out, R;
  wire [9:0] demultiplexer_2_out1;
  wire [25:0] demultiplexer_1_out1, \não_Js , \não_R ;

  and u_R (R, ~\instrução [31], ~\instrução [30], ~\instrução [29], ~\instrução [28], ~\instrução [27], ~\instrução [26]);  // AND_Gate
  and u_J (J, ~\instrução [31], ~\instrução [30], ~\instrução [29], ~\instrução [28], \instrução [27], ~\instrução [26]);  // AND_Gate
  and u_JAL (JAL, ~\instrução [31], ~\instrução [30], ~\instrução [29], ~\instrução [28], \instrução [27], \instrução [26]);  // AND_Gate
  Demultiplexer #(.width(26)) demultiplexer_1 (
    .out0(\não_R ), .out1({demultiplexer_1_out1[25], funct, shamt, rd, demultiplexer_1_out1[9:0]}),
    .in(\instrução [25:0]), .sel(R));  // open: en
  Demultiplexer #(.width(26)) demultiplexer_2 (
    .out1({imm, demultiplexer_2_out1}), .in(\não_Js ), .sel(not_1_out));  // open: out0, en
  not not_1 (not_1_out, R);
  Demultiplexer #(.width(26)) demultiplexer_3 (.out0(\não_Js ), .out1(addr), .in(\não_R ), .sel(or_1_out));  // open: en
  or or_1 (or_1_out, J, JAL);
  assign rs = demultiplexer_1_out1[4:0] | demultiplexer_2_out1[4:0];  // OR_Gate or_2, 5 bits wide
  assign rt = demultiplexer_1_out1[9:5] | demultiplexer_2_out1[9:5];  // OR_Gate or_3, 5 bits wide

  assign opcode = \instrução [31:26];
endmodule
