// Logisim project Extensão de Sinal.circ as structural Verilog: 1 circuit, main circuit Extensão de Bits
module \Extensão_de_Bits  (
  input  [15:0] in_1,
  output [31:0] out_2
);


  assign out_2 = {{17{in_1[15]}}, in_1[14:0]};
endmodule
