// Logisim project Memória de Dados.circ as structural Verilog: 1 circuit, main circuit Memória de Dados
module \Memória_de_Dados  (
  input  [31:0] EL,
  input  [31:0] WD,
  input  MenWrite,
  input  MenRead,
  output [31:0] LD
);

  wire clock_1_out;
  wire [31:0] shifter_1_out;

  Shifter #(.width(32), .shift("lr")) shifter_1 (.in(EL), .\dist (5'b00010), .out(shifter_1_out));
  Clock clock_1 (.out(clock_1_out));
  RAM #(.addrWidth(24), .dataWidth(32), .bus("separate")) ram_1 (
    .addr(shifter_1_out[23:0]), .din(WD), .data(LD), .str(MenWrite), .clk(clock_1_out), .ld(MenRead));  // open: sel, clr
endmodule
