// Logisim project Memória de Instruções.circ as structural Verilog: 1 circuit, main circuit Memória de Instrução
module \Memória_de_Instrução  (
  input  [31:0] \Endereço_da_Instrução ,
  output [31:0] out_2
);

  wire [31:0] shifter_1_out;

  Shifter #(.width(32), .shift("lr")) shifter_1 (.in(\Endereço_da_Instrução ), .\dist (5'b00010), .out(shifter_1_out));
  ROM #(.addrWidth(24), .dataWidth(32)) rom_1 (.addr(shifter_1_out[23:0]), .data(out_2));  // open: sel
endmodule
