// Logisim project Unidade de Controle J I.circ as structural Verilog: 1 circuit, main circuit Unidade de Controle
module Unidade_de_Controle (
  input  [5:0] opcode,
  output Jump,
  output Branch,
  output Link,
  output Bne,
  output ExcOut,
  output MemRead,
  output MTC0,
  output MemToReg,
  output MFC0,
  output RegDst,
  output MemWrite,
  output WriteReg,
  output ALUSrc,
  output [1:0] ALUOp
);

  wire ADDI, J;
  wire [1:0] not_1_out, or_3_out;

  and R (RegDst, ~opcode[5], ~opcode[4], ~opcode[3], ~opcode[2], ~opcode[1], ~opcode[0]);  // AND_Gate
  and u_ADDI (ADDI, ~opcode[5], ~opcode[4], ~opcode[3], ~opcode[2], ~opcode[1], opcode[0]);  // AND_Gate
  and LW (MemRead, ~opcode[5], ~opcode[4], ~opcode[3], ~opcode[2], opcode[1], ~opcode[0]);  // AND_Gate
  and SW (MemWrite, ~opcode[5], ~opcode[4], ~opcode[3], ~opcode[2], opcode[1], opcode[0]);  // AND_Gate
  and BEQ (Branch, ~opcode[5], ~opcode[4], ~opcode[3], opcode[2], ~opcode[1], ~opcode[0]);  // AND_Gate
  and u_BNE (Bne, ~opcode[5], ~opcode[4], ~opcode[3], opcode[2], ~opcode[1], opcode[0]);  // AND_Gate
  and u_J (J, ~opcode[5], ~opcode[4], ~opcode[3], opcode[2], opcode[1], ~opcode[0]);  // AND_Gate
  and JAL (Link, ~opcode[5], ~opcode[4], ~opcode[3], opcode[2], opcode[1], opcode[0]);  // AND_Gate
  and RFE (ExcOut, opcode[5], opcode[4], opcode[3], opcode[2], opcode[1], opcode[0]);
  and u_mtc0 (MTC0, opcode[5], opcode[4], opcode[3], opcode[2], opcode[1], ~opcode[0]);  // AND_Gate
  and mft0 (MFC0, opcode[5], opcode[4], opcode[3], opcode[2], ~opcode[1], opcode[0]);  // AND_Gate
  or or_1 (Jump, J, Link);
  or or_2 (not_1_out[1], ADDI, MemRead, MemWrite);
  or or_3 (or_3_out[0], Branch, Bne);
  not not_1 (not_1_out[0], not_1_out[1]);
  not not_2 (or_3_out[1], or_3_out[0]);
  or or_4 (WriteReg, RegDst, ADDI, MFC0, MemRead, Link);
  or or_5 (ALUSrc, ADDI, MemRead, MemWrite);
  assign ALUOp = ~(not_1_out | or_3_out);  // NOR_Gate nor_1, 2 bits wide

  assign MemToReg = MemRead;

  // Other names for the same wires on the sheet: BEQ = Branch; JAL = Link; LW = MemRead; R = RegDst; RFE = ExcOut;
  //   SW = MemWrite
endmodule
