// Logisim project Unidade de Controle da ULA.circ as structural Verilog: 1 circuit, main circuit Unidade de Controle da ULA
module Unidade_de_Controle_da_ULA (
  input  [5:0] funct,
  input  [1:0] ALUOp,
  output [3:0] Op,
  output JR
);

  wire [5:4] multiplexer_1_out;

  Multiplexer #(.select(2), .width(6)) multiplexer_1 (
    .in0(funct), .in1(6'b000101), .in2(6'b000110), .out({multiplexer_1_out, Op}), .sel(ALUOp));  // open: in3, en
  and and_1 (JR, Op[0], ~Op[1], ~Op[2], Op[3]);  // AND_Gate
endmodule
