// Logisim project Unidade de Controle de Exceções.circ as structural Verilog: 1 circuit, main circuit Controle de Exceções
module \Controle_de_Exceções  (
  input  except,
  input  [31:0] EPC_in,
  input  [4:0] WR_in,
  input  [31:0] resData,
  input  WriteRes,
  output [31:0] EPC_out,
  output [4:0] WR_out,
  output [31:0] MFC0_out
);

  wire or_1_out;

  Register #(.width(32)) EPC (.D(EPC_in), .Q(EPC_out), .clk(except));  // open: en, clr
  Register #(.width(5)) WR (.D(WR_in), .Q(WR_out), .clk(except));  // open: en, clr
  Register #(.width(32)) res (.D(resData), .Q(MFC0_out), .clk(or_1_out));  // open: en, clr
  or or_1 (or_1_out, except, WriteRes);
endmodule
