// Logisim project Datapath Provas.circ as structural Verilog: 11 circuits, main circuit ULA
module main (
  input  in_1
);

  wire ALUSrc, and_1_out, Bne, Branch, button_1_out, button_2_out, Clear, Clock, clock_1_out, Exception,
       ExcOut, Jump, Jump_Register, Link, MemRead, MemToReg, MemWrite, MFC0, MTC0, multiplexer_2_out,
       not_1_out, or_3_out, RegDst, WriteReg, Zero;
  wire [1:0] ALUOp;
  wire [3:0] ucu_1_op;
  wire [4:0] multiplexer_6_out, multiplexer_9_out, rd, rs, rt, shamt, WR, WR_except;
  wire [5:0] funct, opcode;
  wire [15:0] imm;
  wire [25:0] addr;
  wire [31:0] adder_1_out, EPC, imm32, LD1, LD2, \memória_de_dados_1_ld , \memória_de_instrução_1_out_2 ,
       mfc0R, multiplexer_1_out, multiplexer_3_out, multiplexer_4_out, multiplexer_5_out, multiplexer_7_out,
       multiplexer_8_out, multiplexer_11_out, multiplexer_12_out, multiplexer_13_out, multiplexer_14_out,
       n2_conc_1_out_3, PC___4, PC_q, result;

  Button button_1 (.out(button_1_out));
  Clock clock_1 (.out(clock_1_out));
  Button button_2 (.out(button_2_out));
  or or_1 (Clear, in_1, button_1_out);
  or or_2 (Clock, clock_1_out, button_2_out);
  UC uc_1 (
    .opcode(opcode), .Jump(Jump), .Link(Link), .Bne(Bne), .ExcOut(ExcOut), .MemRead(MemRead), .MTC0(MTC0),
    .MemToReg(MemToReg), .MFC0(MFC0), .RegDst(RegDst), .MemWrite(MemWrite), .WriteReg(WriteReg),
    .ALUSrc(ALUSrc), .ALUOp(ALUOp), .Branch(Branch));
  // Probe on {imm32[29:0], 2'b00}
  // Probe on multiplexer_1_out
  Multiplexer #(.width(32)) multiplexer_1 (.in0(LD1), .in1(result), .out(multiplexer_1_out), .sel(MTC0));  // open: en
  // Probe on adder_1_out
  Adder #(.width(32)) adder_1 (.a({imm32[29:0], 2'b00}), .b(PC___4), .out(adder_1_out));  // open: cin, cout
  and and_1 (and_1_out, multiplexer_2_out, Branch);
  Multiplexer multiplexer_2 (.in0(Zero), .in1(not_1_out), .out(multiplexer_2_out), .sel(Bne));  // open: en
  not not_1 (not_1_out, Zero);
  // Probe on PC___4
  // Probe on WR
  // Probe on multiplexer_3_out
  Multiplexer #(.width(32)) multiplexer_3 (
    .in0(PC___4), .in1(adder_1_out), .out(multiplexer_3_out), .sel(and_1_out));  // open: en
  UCE uce_1 (
    .except(Exception), .EPC_in(PC___4), .WR_in(WR), .resData(multiplexer_1_out), .WriteRes(MTC0),
    .EPC_out(EPC), .WR_out(WR_except), .MFC0_out(mfc0R), .Clock(Clock));
  Multiplexer #(.width(32)) multiplexer_4 (
    .in0(multiplexer_3_out), .in1(LD1), .out(multiplexer_4_out), .sel(Jump_Register));  // open: en
  // Probe on EPC
  // Probe on mfc0R
  // Probe on WR_except
  // Probe on multiplexer_4_out
  _2_conc u_2_conc_1 (.addr(addr), .PC_4(PC___4), .out_3(n2_conc_1_out_3));
  // Probe on multiplexer_5_out
  Multiplexer #(.width(32)) multiplexer_5 (
    .in0(multiplexer_4_out), .in1(n2_conc_1_out_3), .out(multiplexer_5_out), .sel(Jump));  // open: en
  Multiplexer #(.width(5)) multiplexer_6 (.in0(rt), .in1(rd), .out(multiplexer_6_out), .sel(RegDst));  // open: en
  Multiplexer #(.width(32)) multiplexer_7 (
    .in0(multiplexer_5_out), .in1(32'hffeff0), .out(multiplexer_7_out), .sel(Exception));  // open: en
  // Probe on multiplexer_6_out
  // Probe on multiplexer_7_out
  Multiplexer #(.width(32)) multiplexer_8 (
    .in0(multiplexer_7_out), .in1(EPC), .out(multiplexer_8_out), .sel(ExcOut));  // open: en
  // Probe on multiplexer_9_out
  // Probe on WR
  Multiplexer #(.width(5)) multiplexer_9 (
    .in0(multiplexer_6_out), .in1(WR_except), .out(multiplexer_9_out), .sel(ExcOut));  // open: en
  Multiplexer #(.width(5)) multiplexer_10 (.in0(multiplexer_9_out), .in1({5{1'b1}}), .out(WR), .sel(Link));  // open: en
  Multiplexer #(.width(32)) multiplexer_11 (
    .in0(multiplexer_14_out), .in1(mfc0R), .out(multiplexer_11_out), .sel(or_3_out));  // open: en
  or or_3 (or_3_out, ExcOut, MFC0);
  // Probe on multiplexer_8_out
  // Probe on WR
  Multiplexer #(.width(32)) multiplexer_12 (
    .in0(multiplexer_11_out), .in1(PC___4), .out(multiplexer_12_out), .sel(Link));  // open: en
  // Probe on multiplexer_11_out
  Adder #(.width(32)) adder_2 (.a(32'h4), .b(PC_q), .out(PC___4));  // open: cin, cout
  Register #(.width(32)) PC (.D(multiplexer_8_out), .en(1'b1), .Q(PC_q), .clk(Clock), .clr(Clear));
  // Probe on multiplexer_12_out
  // Probe on PC___4
  Banco_de_Registradores banco_de_registradores_1 (
    .WR(WR), .WD(multiplexer_12_out), .LD1(LD1), .LR1(rs), .LD2(LD2), .LR2(rt), .RegWrite(WriteReg),
    .Clock(Clock), .Clear(Clear));
  \Extensão_de_Sinal  \extensão_de_sinal_1  (.in_1(imm), .out_2(imm32));
  // Probe on multiplexer_14_out
  \Memória_de_Instrução  \memória_de_instrução_1  (
    .\Endereço_da_Instrução (PC_q), .out_2(\memória_de_instrução_1_out_2 ));
  // Probe on LD1
  // Probe on multiplexer_13_out
  Multiplexer #(.width(32)) multiplexer_13 (
    .in0(LD2), .in1(imm32), .out(multiplexer_13_out), .sel(ALUSrc));  // open: en
  UCU ucu_1 (.funct(funct), .ALUOp(ALUOp), .JR(Jump_Register), .Op(ucu_1_op));
  ULA ula_1 (
    .A(LD1), .B(multiplexer_13_out), .\Operação_ALU (ucu_1_op), .Result(result), .Overflow(Exception),
    .shamt(shamt), .ZERO(Zero));
  // Probe on ucu_1_op
  Multiplexer #(.width(32)) multiplexer_14 (
    .in0(result), .in1(\memória_de_dados_1_ld ), .out(multiplexer_14_out), .sel(MemToReg));  // open: en
  // Probe on \memória_de_instrução_1_out_2 
  // Probe on result
  \Decodificador_de_Instrução  \decodificador_de_instrução_1  (
    .\instrução (\memória_de_instrução_1_out_2 ), .opcode(opcode), .addr(addr), .rs(rs), .rt(rt),
    .funct(funct), .shamt(shamt), .rd(rd), .imm(imm));
  \Memória_de_Dados  \memória_de_dados_1  (
    .EL(result), .WD(LD2), .MenWrite(MemWrite), .MenRead(MemRead), .LD(\memória_de_dados_1_ld ),
    .Clock(Clock), .Clear(Clear));
  // Probe on opcode
  // Probe on rs
  // Probe on rt
  // Probe on rd
  // Probe on shamt
  // Probe on funct
  // Probe on imm
  // Probe on addr
  // Probe on \memória_de_dados_1_ld 
endmodule

module ULA (
  input  [31:0] A,
  input  [31:0] B,
  input  [3:0] \Operação_ALU ,
  input  [4:0] shamt,
  output ZERO,
  output [31:0] Result,
  output Overflow
);

  wire and_2_out, and_3_out, and_4_out, and_5_out, and_6_out, and_7_out, and_8_out, and_9_out, or_2_out,
       or_3_out, or_4_out, or_5_out;
  wire [0:0] SLT;
  wire [31:0] ADD, AND, NOR, OR, SLL, SRL, SUB, XOR;

  assign AND = A & B;  // AND_Gate and_1, 32 bits wide
  assign OR = A | B;  // OR_Gate or_1, 32 bits wide
  assign NOR = ~(A | B);  // NOR_Gate nor_1, 32 bits wide
  assign XOR = A ^ B;  // XOR_Gate xor_1, 32 bits wide
  Comparator #(.width(32)) comparator_1 (.a(A), .b(B), .lt(SLT[0]));  // open: gt, eq
  Adder #(.width(32)) adder_1 (.a(A), .b(B), .out(ADD));  // open: cin, cout
  Subtractor #(.width(32)) subtractor_1 (.a(A), .b(B), .out(SUB));  // open: bin, bout
  Shifter #(.width(32)) shifter_1 (.in(B), .\dist (shamt), .out(SLL));
  Shifter #(.width(32), .shift("lr")) shifter_2 (.in(B), .\dist (shamt), .out(SRL));
  and and_2 (and_2_out, ~A[31], ~B[31], Result[31]);  // AND_Gate
  and and_3 (and_3_out, A[31], B[31], ~Result[31]);  // AND_Gate
  and and_4 (and_4_out, ~A[31], B[31], Result[31]);  // AND_Gate
  and and_5 (and_5_out, A[31], ~B[31], ~Result[31]);  // AND_Gate
  Comparator #(.width(32)) comparator_2 (.a({32{1'b0}}), .b(Result), .eq(ZERO));  // open: gt, lt
  Multiplexer #(.select(4), .width(32)) multiplexer_1 (
    .in0(ADD), .in1(SLL), .in2(SUB), .in3(SRL), .in4(AND), .in5(OR), .in6(XOR), .in7(NOR), .in9({32{1'b0}}),
    .in10({{31{1'b0}}, SLT[0]}), .out(Result), .sel(\Operação_ALU ));  // open: in8, in11, in12, in13, in14, in15, en
  // Probe on \Operação_ALU 
  or or_2 (or_2_out, and_2_out, and_3_out);
  or or_3 (or_3_out, and_4_out, and_5_out);
  and and_6 (and_6_out, or_2_out, ~\Operação_ALU [1]);  // AND_Gate
  or or_4 (or_4_out, and_6_out, and_7_out);
  and and_7 (and_7_out, \Operação_ALU [1], or_3_out);
  and and_8 (and_8_out, ~\Operação_ALU [3], ~\Operação_ALU [2], ~\Operação_ALU [1], ~\Operação_ALU [0]);  // AND_Gate
  or or_5 (or_5_out, and_8_out, and_9_out);
  and and_9 (and_9_out, ~\Operação_ALU [3], ~\Operação_ALU [2], \Operação_ALU [1], ~\Operação_ALU [0]);  // AND_Gate
  and and_10 (Overflow, or_4_out, or_5_out);

  // Other names for the same wires on the sheet: op[3:0] = \Operação_ALU ; res[31:0] = Result

  // Notes on the sheet:
  //   lógicas
  //   aritiméticas
  //   0
  //   1
  //   2
  //   3
  //   4
  //   5
  //   6
  //   7
  //   9
  //   10
endmodule

module Banco_de_Registradores (
  input  [4:0] WR,
  input  [31:0] WD,
  input  RegWrite,
  input  Clock,
  input  Clear,
  input  [4:0] LR1,
  input  [4:0] LR2,
  output [31:0] LD1,
  output [31:0] LD2
);

  wire and_1_out, and_2_out, and_3_out, and_4_out, and_5_out, and_6_out, and_7_out, and_8_out, and_9_out,
       and_10_out, and_11_out, and_12_out, and_13_out, and_14_out, and_15_out, and_16_out, and_17_out,
       and_18_out, and_19_out, and_20_out, and_21_out, and_22_out, and_23_out, and_24_out, and_25_out,
       and_26_out, and_27_out, and_28_out, and_29_out, and_30_out, and_31_out, demultiplexer_1_out1,
       demultiplexer_1_out2, demultiplexer_1_out3, demultiplexer_1_out4, demultiplexer_1_out5,
       demultiplexer_1_out6, demultiplexer_1_out7, demultiplexer_1_out8, demultiplexer_1_out9,
       demultiplexer_1_out10, demultiplexer_1_out11, demultiplexer_1_out12, demultiplexer_1_out13,
       demultiplexer_1_out14, demultiplexer_1_out15, demultiplexer_1_out16, demultiplexer_1_out17,
       demultiplexer_1_out18, demultiplexer_1_out19, demultiplexer_1_out20, demultiplexer_1_out21,
       demultiplexer_1_out22, demultiplexer_1_out23, demultiplexer_1_out24, demultiplexer_1_out25,
       demultiplexer_1_out26, demultiplexer_1_out27, demultiplexer_1_out28, demultiplexer_1_out29,
       demultiplexer_1_out30, demultiplexer_1_out31;
  wire [31:0] _0, _1, _2, _3, _4, _5, _6, _7, _8, _9, _10, _11, _12, _13, _14, _15, _16, _17, _18, _19, _20,
       _21, _22, _23, _24, _25, _26, _27, _28, _29, _30, _31;

  Register #(.width(32)) register_1 (.Q(_0));  // open: D, en, clk, clr
  Demultiplexer #(.select(5)) demultiplexer_1 (
    .out1(demultiplexer_1_out1), .out2(demultiplexer_1_out2), .out3(demultiplexer_1_out3),
    .out4(demultiplexer_1_out4), .out5(demultiplexer_1_out5), .out6(demultiplexer_1_out6),
    .out7(demultiplexer_1_out7), .out8(demultiplexer_1_out8), .out9(demultiplexer_1_out9),
    .out10(demultiplexer_1_out10), .out11(demultiplexer_1_out11), .out12(demultiplexer_1_out12),
    .out13(demultiplexer_1_out13), .out14(demultiplexer_1_out14), .out15(demultiplexer_1_out15),
    .out16(demultiplexer_1_out16), .out17(demultiplexer_1_out17), .out18(demultiplexer_1_out18),
    .out19(demultiplexer_1_out19), .out20(demultiplexer_1_out20), .out21(demultiplexer_1_out21),
    .out22(demultiplexer_1_out22), .out23(demultiplexer_1_out23), .out24(demultiplexer_1_out24),
    .out25(demultiplexer_1_out25), .out26(demultiplexer_1_out26), .out27(demultiplexer_1_out27),
    .out28(demultiplexer_1_out28), .out29(demultiplexer_1_out29), .out30(demultiplexer_1_out30),
    .out31(demultiplexer_1_out31), .in(1'b1), .sel(WR));  // open: out0, en
  and and_1 (and_1_out, RegWrite, demultiplexer_1_out1);
  and and_2 (and_2_out, demultiplexer_1_out31, RegWrite);
  Register #(.width(32)) register_2 (.D(WD), .en(and_1_out), .Q(_1), .clk(Clock), .clr(Clear));
  and and_3 (and_3_out, RegWrite, demultiplexer_1_out2);
  Register #(.width(32)) register_3 (.D(WD), .en(and_2_out), .Q(_31), .clk(Clock), .clr(Clear));
  and and_4 (and_4_out, demultiplexer_1_out30, RegWrite);
  Register #(.width(32)) register_4 (.D(WD), .en(and_3_out), .Q(_2), .clk(Clock), .clr(Clear));
  and and_5 (and_5_out, RegWrite, demultiplexer_1_out3);
  Register #(.width(32)) register_5 (.D(WD), .en(and_4_out), .Q(_30), .clk(Clock), .clr(Clear));
  and and_6 (and_6_out, demultiplexer_1_out29, RegWrite);
  Register #(.width(32)) register_6 (.D(WD), .en(and_5_out), .Q(_3), .clk(Clock), .clr(Clear));
  and and_7 (and_7_out, RegWrite, demultiplexer_1_out4);
  Register #(.width(32)) register_7 (.D(WD), .en(and_6_out), .Q(_29), .clk(Clock), .clr(Clear));
  Register #(.width(32)) register_8 (.D(WD), .en(and_7_out), .Q(_4), .clk(Clock), .clr(Clear));
  Register #(.width(32)) register_9 (.D(WD), .en(and_8_out), .Q(_28), .clk(Clock), .clr(Clear));
  and and_8 (and_8_out, demultiplexer_1_out28, RegWrite);
  Register #(.width(32)) register_10 (.D(WD), .en(and_9_out), .Q(_5), .clk(Clock), .clr(Clear));
  and and_9 (and_9_out, RegWrite, demultiplexer_1_out5);
  Register #(.width(32)) register_11 (.D(WD), .en(and_10_out), .Q(_27), .clk(Clock), .clr(Clear));
  and and_10 (and_10_out, demultiplexer_1_out27, RegWrite);
  Register #(.width(32)) register_12 (.D(WD), .en(and_11_out), .Q(_6), .clk(Clock), .clr(Clear));
  and and_11 (and_11_out, RegWrite, demultiplexer_1_out6);
  Register #(.width(32)) register_13 (.D(WD), .en(and_12_out), .Q(_26), .clk(Clock), .clr(Clear));
  and and_12 (and_12_out, demultiplexer_1_out26, RegWrite);
  Register #(.width(32)) register_14 (.D(WD), .en(and_13_out), .Q(_7), .clk(Clock), .clr(Clear));
  and and_13 (and_13_out, RegWrite, demultiplexer_1_out7);
  Register #(.width(32)) register_15 (.D(WD), .en(and_14_out), .Q(_25), .clk(Clock), .clr(Clear));
  and and_14 (and_14_out, demultiplexer_1_out25, RegWrite);
  and and_15 (and_15_out, RegWrite, demultiplexer_1_out8);
  and and_16 (and_16_out, demultiplexer_1_out24, RegWrite);
  Register #(.width(32)) register_16 (.D(WD), .en(and_15_out), .Q(_8), .clk(Clock), .clr(Clear));
  and and_17 (and_17_out, RegWrite, demultiplexer_1_out9);
  Register #(.width(32)) register_17 (.D(WD), .en(and_16_out), .Q(_24), .clk(Clock), .clr(Clear));
  and and_18 (and_18_out, demultiplexer_1_out23, RegWrite);
  Register #(.width(32)) register_18 (.D(WD), .en(and_17_out), .Q(_9), .clk(Clock), .clr(Clear));
  and and_19 (and_19_out, RegWrite, demultiplexer_1_out10);
  Register #(.width(32)) register_19 (.D(WD), .en(and_18_out), .Q(_23), .clk(Clock), .clr(Clear));
  and and_20 (and_20_out, demultiplexer_1_out22, RegWrite);
  Multiplexer #(.select(5), .width(32)) multiplexer_1 (
    .in0(_0), .in1(_1), .in2(_2), .in3(_3), .in4(_4), .in5(_5), .in6(_6), .in7(_7), .in8(_8), .in9(_9),
    .in10(_10), .in11(_11), .in12(_12), .in13(_13), .in14(_14), .in15(_15), .in16(_16), .in17(_17),
    .in18(_18), .in19(_19), .in20(_20), .in21(_21), .in22(_22), .in23(_23), .in24(_24), .in25(_25),
    .in26(_26), .in27(_27), .in28(_28), .in29(_29), .in30(_30), .in31(_31), .out(LD1), .sel(LR1));  // open: en
  Multiplexer #(.select(5), .width(32)) multiplexer_2 (
    .in0(_0), .in1(_1), .in2(_2), .in3(_3), .in4(_4), .in5(_5), .in6(_6), .in7(_7), .in8(_8), .in9(_9),
    .in10(_10), .in11(_11), .in12(_12), .in13(_13), .in14(_14), .in15(_15), .in16(_16), .in17(_17),
    .in18(_18), .in19(_19), .in20(_20), .in21(_21), .in22(_22), .in23(_23), .in24(_24), .in25(_25),
    .in26(_26), .in27(_27), .in28(_28), .in29(_29), .in30(_30), .in31(_31), .out(LD2), .sel(LR2));  // open: en
  Register #(.width(32)) register_20 (.D(WD), .en(and_19_out), .Q(_10), .clk(Clock), .clr(Clear));
  and and_21 (and_21_out, RegWrite, demultiplexer_1_out11);
  Register #(.width(32)) register_21 (.D(WD), .en(and_20_out), .Q(_22), .clk(Clock), .clr(Clear));
  and and_22 (and_22_out, demultiplexer_1_out21, RegWrite);
  Register #(.width(32)) register_22 (.D(WD), .en(and_21_out), .Q(_11), .clk(Clock), .clr(Clear));
  and and_23 (and_23_out, RegWrite, demultiplexer_1_out12);
  Register #(.width(32)) register_23 (.D(WD), .en(and_22_out), .Q(_21), .clk(Clock), .clr(Clear));
  Register #(.width(32)) register_24 (.D(WD), .en(and_23_out), .Q(_12), .clk(Clock), .clr(Clear));
  Register #(.width(32)) register_25 (.D(WD), .en(and_24_out), .Q(_20), .clk(Clock), .clr(Clear));
  and and_24 (and_24_out, demultiplexer_1_out20, RegWrite);
  Register #(.width(32)) register_26 (.D(WD), .en(and_25_out), .Q(_13), .clk(Clock), .clr(Clear));
  and and_25 (and_25_out, RegWrite, demultiplexer_1_out13);
  Register #(.width(32)) register_27 (.D(WD), .en(and_26_out), .Q(_19), .clk(Clock), .clr(Clear));
  and and_26 (and_26_out, demultiplexer_1_out19, RegWrite);
  Register #(.width(32)) register_28 (.D(WD), .en(and_27_out), .Q(_14), .clk(Clock), .clr(Clear));
  and and_27 (and_27_out, RegWrite, demultiplexer_1_out14);
  Register #(.width(32)) register_29 (.D(WD), .en(and_28_out), .Q(_18), .clk(Clock), .clr(Clear));
  and and_28 (and_28_out, demultiplexer_1_out18, RegWrite);
  Register #(.width(32)) register_30 (.D(WD), .en(and_29_out), .Q(_15), .clk(Clock), .clr(Clear));
  and and_29 (and_29_out, RegWrite, demultiplexer_1_out15);
  Register #(.width(32)) register_31 (.D(WD), .en(and_30_out), .Q(_17), .clk(Clock), .clr(Clear));
  and and_30 (and_30_out, demultiplexer_1_out17, RegWrite);
  and and_31 (and_31_out, demultiplexer_1_out16, RegWrite);
  Register #(.width(32)) register_32 (.D(WD), .en(and_31_out), .Q(_16), .clk(Clock), .clr(Clear));

  // Other names for the same wires on the sheet: Reg_Write = RegWrite
endmodule

module \Memória_de_Dados  (
  input  [31:0] EL,
  input  [31:0] WD,
  input  Clock,
  input  Clear,
  input  MenWrite,
  input  MenRead,
  output [31:0] LD
);

  wire [31:0] shifter_1_out;

  Shifter #(.width(32), .shift("lr")) shifter_1 (.in(EL), .\dist (5'b00010), .out(shifter_1_out));
  RAM #(.addrWidth(24), .dataWidth(32), .bus("separate")) ram_1 (
    .addr(shifter_1_out[23:0]), .din(WD), .data(LD), .str(MenWrite), .clk(Clock), .ld(MenRead), .clr(Clear));  // open: sel
endmodule

module \Memória_de_Instrução  (
  input  [31:0] \Endereço_da_Instrução ,
  output [31:0] out_2
);

  wire [31:0] shifter_1_out;

  Shifter #(.width(32), .shift("lr")) shifter_1 (.in(\Endereço_da_Instrução ), .\dist (5'b00010), .out(shifter_1_out));
  ROM #(.addrWidth(24), .dataWidth(32)) rom_1 (.addr(shifter_1_out[23:0]), .data(out_2));  // open: sel

  // Notes on the sheet:
  //   contents of rom_1 (hex, n*v repeats v):
  //   8000009 8f290000 8f2a0004 12a582a 11600002 21290001 8000003 af290000 3e00008 20080001 af280000
  //   20080003 af280004 20080045 af280008 2008000b af28000c c000001 8f290000 1094022 8f2b0008 10b5026
  //   a50c2 10a6025 18b6024
endmodule

module \Decodificador_de_Instrução  (
  input  [31:0] \instrução ,
  output [5:0] funct,
  output [4:0] shamt,
  output [4:0] rd,
  output [4:0] rt,
  output [4:0] rs,
  output [15:0] imm,
  output [25:0] addr,
  output [5:0] opcode
);

  wire J, JAL, not_1_out, or_1_out, R;
  wire [25:0] \não_Js , \não_R ;
  wire [25:16] demultiplexer_1_out1, demultiplexer_2_out1;

  and u_R (R, ~\instrução [31], ~\instrução [30], ~\instrução [29], ~\instrução [28], ~\instrução [27], ~\instrução [26]);  // AND_Gate
  and u_J (J, ~\instrução [31], ~\instrução [30], ~\instrução [29], ~\instrução [28], \instrução [27], ~\instrução [26]);  // AND_Gate
  and u_JAL (JAL, ~\instrução [31], ~\instrução [30], ~\instrução [29], ~\instrução [28], \instrução [27], \instrução [26]);  // AND_Gate
  Demultiplexer #(.width(26)) demultiplexer_1 (
    .out0(\não_R ), .out1({demultiplexer_1_out1, rd, shamt, funct}), .in(\instrução [25:0]), .sel(R));  // open: en
  Demultiplexer #(.width(26)) demultiplexer_2 (
    .out1({demultiplexer_2_out1, imm}), .in(\não_Js ), .sel(not_1_out));  // open: out0, en
  not not_1 (not_1_out, R);
  Demultiplexer #(.width(26)) demultiplexer_3 (.out0(\não_Js ), .out1(addr), .in(\não_R ), .sel(or_1_out));  // open: en
  or or_1 (or_1_out, J, JAL);
  assign rt = demultiplexer_1_out1[20:16] | demultiplexer_2_out1[20:16];  // OR_Gate or_2, 5 bits wide
  assign rs = demultiplexer_1_out1[25:21] | demultiplexer_2_out1[25:21];  // OR_Gate or_3, 5 bits wide

  assign opcode = \instrução [31:26];
endmodule

module UC (
  input  [5:0] opcode,
  output Jump,
  output Branch,
  output Link,
  output Bne,
  output ExcOut,
  output MemRead,
  output MTC0,
  output MemToReg,
  output MFC0,
  output RegDst,
  output MemWrite,
  output WriteReg,
  output ALUSrc,
  output [1:0] ALUOp
);

  wire ADDI, BEQ, J;
  wire [1:0] not_1_out, or_4_out;

  and R (RegDst, ~opcode[5], ~opcode[4], ~opcode[3], ~opcode[2], ~opcode[1], ~opcode[0]);  // AND_Gate
  and u_ADDI (ADDI, ~opcode[5], ~opcode[4], opcode[3], ~opcode[2], ~opcode[1], ~opcode[0]);  // AND_Gate
  and LW (MemRead, opcode[5], ~opcode[4], ~opcode[3], ~opcode[2], opcode[1], opcode[0]);  // AND_Gate
  and SW (MemWrite, opcode[5], ~opcode[4], opcode[3], ~opcode[2], opcode[1], opcode[0]);  // AND_Gate
  and u_BEQ (BEQ, ~opcode[5], ~opcode[4], ~opcode[3], opcode[2], ~opcode[1], ~opcode[0]);  // AND_Gate
  and u_BNE (Bne, ~opcode[5], ~opcode[4], ~opcode[3], opcode[2], ~opcode[1], opcode[0]);  // AND_Gate
  and u_J (J, ~opcode[5], ~opcode[4], ~opcode[3], ~opcode[2], opcode[1], ~opcode[0]);  // AND_Gate
  and JAL (Link, ~opcode[5], ~opcode[4], ~opcode[3], ~opcode[2], opcode[1], opcode[0]);  // AND_Gate
  and RFE (ExcOut, opcode[5], opcode[4], opcode[3], opcode[2], opcode[1], opcode[0]);
  and u_mtc0 (MTC0, opcode[5], opcode[4], opcode[3], opcode[2], opcode[1], ~opcode[0]);  // AND_Gate
  and mft0 (MFC0, opcode[5], opcode[4], opcode[3], opcode[2], ~opcode[1], opcode[0]);  // AND_Gate
  or or_1 (Jump, J, Link);
  or or_2 (Branch, BEQ, Bne);
  or or_3 (not_1_out[1], ADDI, MemRead, MemWrite);
  or or_4 (or_4_out[0], BEQ, Bne);
  not not_1 (not_1_out[0], not_1_out[1]);
  not not_2 (or_4_out[1], or_4_out[0]);
  or or_5 (WriteReg, RegDst, ADDI, MFC0, MemRead, Link);
  or or_6 (ALUSrc, ADDI, MemRead, MemWrite);
  assign ALUOp = ~(not_1_out | or_4_out);  // NOR_Gate nor_1, 2 bits wide

  assign MemToReg = MemRead;

  // Other names for the same wires on the sheet: JAL = Link; LW = MemRead; R = RegDst; RFE = ExcOut; SW = MemWrite
endmodule

module UCU (
  input  [5:0] funct,
  input  [1:0] ALUOp,
  output [3:0] Op,
  output JR
);

  wire [0:0] not_1_out;
  wire [5:0] multiplexer_1_out;
  wire [5:4] adder_1_out;

  Multiplexer #(.select(2), .width(6)) multiplexer_1 (
    .in0(funct), .in1(6'b100000), .in2(6'b100010), .out(multiplexer_1_out), .sel(ALUOp));  // open: in3, en
  and and_1 (JR, ~multiplexer_1_out[0], ~multiplexer_1_out[1], ~multiplexer_1_out[2], multiplexer_1_out[3]);  // AND_Gate
  not not_1 (not_1_out[0], multiplexer_1_out[5]);
  Adder #(.width(6)) adder_1 (
    .a({{5{1'b0}}, not_1_out[0]}), .b(multiplexer_1_out), .out({adder_1_out, Op}));  // open: cin, cout
endmodule

module UCE (
  input  except,
  input  [31:0] EPC_in,
  input  [4:0] WR_in,
  input  [31:0] resData,
  input  WriteRes,
  input  Clock,
  output [31:0] EPC_out,
  output [4:0] WR_out,
  output [31:0] MFC0_out
);

  wire or_1_out;

  or or_1 (or_1_out, except, WriteRes);
  Register #(.width(32)) EPC (.D(EPC_in), .en(except), .Q(EPC_out), .clk(Clock));  // open: clr
  Register #(.width(5)) WR (.D(WR_in), .en(except), .Q(WR_out), .clk(Clock));  // open: clr
  Register #(.width(32)) res (.D(resData), .en(or_1_out), .Q(MFC0_out), .clk(Clock));  // open: clr
endmodule

module \Extensão_de_Sinal  (
  input  [15:0] in_1,
  output [31:0] out_2
);


  assign out_2 = {{17{in_1[15]}}, in_1[14:0]};
endmodule

module _2_conc (
  input  [25:0] addr,
  input  [31:0] PC_4,
  output [31:0] out_3
);


  assign out_3 = {PC_4[31:28], addr, 2'b00};
endmodule
